// Logisim project CPU.circ as structural Verilog: 1 circuit, main circuit CPU
module CPU (
  input  in_1,
  input  Clock
);

  wire not_1_out, not_2_out, not_3_out;
  wire [3:0] Decode_opcode, ID_EX_opcode_2;
  wire [4:0] Decode_rd, Decode_rt, Decode_shift, Fetch_clock_2, ID_EX_clock_data_2, ID_EX_rd_2, ID_EX_rt_2,
       ID_EX_shift_2, IF_ID_clock_data_2;
  wire [15:0] Decode_immediate, ID_EX_immediate_2;
  wire [31:0] Decode_a, Decode_b, Fetch_instructions, ID_EX_a_2, ID_EX_b_2, IF_ID_instructions_data_2,
       undriven;

  Fetch Fetch (.Clock(not_1_out), .Instructions(Fetch_instructions), .Clock_2(Fetch_clock_2));
  not not_1 (not_1_out, Clock);
  Decode Decode (
    .D(undriven), .Instruction(IF_ID_instructions_data_2), .Clock(not_2_out), .OpCode(Decode_opcode),
    .Shift(Decode_shift), .A(Decode_a), .B(Decode_b), .Immediate(Decode_immediate), .RT(Decode_rt),
    .RD(Decode_rd));
  IF_ID IF_ID (
    .Instructions_Data(Fetch_instructions), .Clock_Data(Fetch_clock_2), .Clock(Clock),
    .Instructions_Data_2(IF_ID_instructions_data_2), .Clock_Data_2(IF_ID_clock_data_2));
  not not_2 (not_2_out, Clock);
  ID_EX ID_EX (
    .OpCode(Decode_opcode), .Shift(Decode_shift), .A(Decode_a), .B(Decode_b), .Immediate(Decode_immediate),
    .RT(Decode_rt), .RD(Decode_rd), .Clock_Data(IF_ID_clock_data_2), .Clock(Clock),
    .OpCode_2(ID_EX_opcode_2), .Shift_2(ID_EX_shift_2), .A_2(ID_EX_a_2), .B_2(ID_EX_b_2),
    .Immediate_2(ID_EX_immediate_2), .RT_2(ID_EX_rt_2), .RD_2(ID_EX_rd_2), .Clock_Data_2(ID_EX_clock_data_2));
  Execute Execute (
    .OpCode(ID_EX_opcode_2), .Shift(ID_EX_shift_2), .A(ID_EX_a_2), .B(ID_EX_b_2),
    .Immediate(ID_EX_immediate_2), .RT(ID_EX_rt_2), .RD(ID_EX_rd_2), .Clock_Data(ID_EX_clock_data_2),
    .Clock(not_3_out), .UI(in_1));  // open: A_2, D, B_2, Target, OpCode_2, RT_2, RD_2
  not not_3 (not_3_out, Clock);
endmodule
